// Digital circuit 2-bit-multiplier.dig as structural Verilog
module _2_bit_multiplier (
  input  in_1,
  input  in_2,
  input  in_3,
  input  in_4,
  output P3,
  output P2,
  output P1,
  output P0
);

  wire and_2_out, and_3_out, and_4_out, half_adder_1_p4;

  and and_1 (P0, in_2, in_4);
  and and_2 (and_2_out, in_1, in_4);
  and and_3 (and_3_out, in_3, in_2);
  and and_4 (and_4_out, in_3, in_1);
  // half_adder half_adder_1: pin names not known; wires that end beside it: and_2_out, and_3_out, P1, half_adder_1_p4
  // half_adder half_adder_2: pin names not known; wires that end beside it: half_adder_1_p4, and_4_out, P2, P3
endmodule
