// Digital circuit 4_bit_ripple.dig as structural Verilog
module _4_bit_ripple (
  input  [3:0] A,
  input  [3:0] B,
  input  carry_in,
  output [3:0] sum,
  output carry_out
);

  wire _1_bit_adder_2_c_o, _1_bit_adder_3_c_o, _1_bit_adder_4_c_o;

  Add _1_bit_adder (.a(A[3]), .b(B[3]), .c_i(_1_bit_adder_2_c_o), .s(sum[3]), .c_o(carry_out));
  Add _1_bit_adder_2 (.a(A[2]), .b(B[2]), .c_i(_1_bit_adder_3_c_o), .s(sum[2]), .c_o(_1_bit_adder_2_c_o));
  Add _1_bit_adder_3 (.a(A[1]), .b(B[1]), .c_i(_1_bit_adder_4_c_o), .s(sum[1]), .c_o(_1_bit_adder_3_c_o));
  Add _1_bit_adder_4 (.a(A[0]), .b(B[0]), .c_i(carry_in), .s(sum[0]), .c_o(_1_bit_adder_4_c_o));
  // Pins of 1 and 4 bits meet at A
  // Pins of 1 and 4 bits meet at B
  // Pins of 1 and 4 bits meet at sum
endmodule
